// Logisim project 6651071080_LAB1_bai1.circ as structural Verilog: 1 circuit, main circuit main
module main (
  input  EN,
  input  A2,
  input  A1,
  input  A0,
  output Y0,
  output Y1,
  output Y2,
  output Y3,
  output Y4,
  output Y5,
  output Y6,
  output Y7
);

  wire not_1_out, not_2_out, not_3_out, undriven, undriven_2, undriven_3, undriven_4, undriven_5, undriven_6,
       undriven_7, undriven_8, undriven_9, undriven_10, undriven_11, undriven_12, undriven_13, undriven_14,
       undriven_15, undriven_16, undriven_17, undriven_18, undriven_19, undriven_20, undriven_21,
       undriven_22, undriven_23, undriven_24, undriven_25, undriven_26, undriven_27, undriven_28;

  not not_1 (not_1_out, undriven);
  not not_2 (not_2_out, undriven_2);
  not not_3 (not_3_out, undriven_3);
  and and_1 (Y0, undriven_4, undriven_14, undriven_20, undriven_26);
  and and_2 (Y1, undriven_5, undriven_15, undriven_21, undriven_23);
  and and_3 (Y2, undriven_6, undriven_16, undriven_17, undriven_27);
  and and_4 (Y3, undriven_7, not_1_out, undriven_18, undriven_24);
  and and_5 (Y4, undriven_8, undriven_11, undriven_22, undriven_28);
  and and_6 (Y5, undriven_9, undriven_12, not_2_out, undriven_25);
  and and_7 (Y6, undriven_10, undriven_13, undriven_19, not_3_out);
  and and_8 (Y7, EN, A2, A1, A0);

  // Notes on the sheet:
  //   Nguyễn Thị Huyền Trân_6651071080
endmodule
