// Logisim project 6651071080_LAB1_bai3.circ as structural Verilog: 1 circuit, main circuit main
module main (
  input  A3,
  input  A2,
  input  A1,
  input  A0,
  input  B3,
  input  B2,
  input  B1,
  input  B0,
  output S3,
  output S2,
  output S1,
  output S0,
  output Cout
);

  wire and_1_out, and_2_out, and_3_out, and_4_out, and_5_out, and_6_out, and_7_out, and_8_out, or_2_out,
       or_3_out, or_4_out, undriven, undriven_2, undriven_3, undriven_4, undriven_5, undriven_6, undriven_7,
       undriven_8, undriven_9, undriven_10, undriven_11, undriven_12, xor_1_out, xor_3_out, xor_5_out,
       xor_7_out;

  xor xor_1 (xor_1_out, A3, B3);
  and and_1 (and_1_out, undriven, undriven_2);
  xor xor_2 (S3, xor_1_out, or_2_out);
  and and_2 (and_2_out, xor_1_out, undriven_3);
  or or_1 (Cout, and_1_out, and_2_out);
  xor xor_3 (xor_3_out, A2, B2);
  and and_3 (and_3_out, undriven_4, undriven_5);
  xor xor_4 (S2, xor_3_out, or_3_out);
  and and_4 (and_4_out, xor_3_out, undriven_6);
  or or_2 (or_2_out, and_3_out, and_4_out);
  xor xor_5 (xor_5_out, A1, B1);
  and and_5 (and_5_out, undriven_7, undriven_8);
  xor xor_6 (S1, xor_5_out, or_4_out);
  and and_6 (and_6_out, xor_5_out, undriven_9);
  or or_3 (or_3_out, and_5_out, and_6_out);
  xor xor_7 (xor_7_out, A0, B0);
  and and_7 (and_7_out, undriven_10, undriven_11);
  xor xor_8 (S0, xor_7_out, 1'b0);
  and and_8 (and_8_out, xor_7_out, undriven_12);
  or or_4 (or_4_out, and_7_out, and_8_out);

  // Notes on the sheet:
  //   Nguyễn Thị Huyền Trân_6651071080
endmodule
