// Logisim project NguyenThiHuyenTran_6651071080_3a.circ as structural Verilog: 2 circuits, main circuit main
module main (
  input  E,
  input  D,
  output out_3
);

  D_Flip_Flop #(.trigger("high")) d_ff_1 (
    .clk(E), .D(D), .Q(out_3), .preset(1'b0), .en(1'b1), .reset(1'b0));  // open: Qn
endmodule

module bct_3a (
  input  E,
  input  D,
  output Q
);

  wire and_1_out, and_2_out, not_1_out, not_2_out;

  not not_1 (not_1_out, E);
  not not_2 (not_2_out, D);
  and and_1 (and_1_out, not_1_out, not_2_out);
  and and_2 (and_2_out, E, D);
  or or_1 (Q, and_1_out, and_2_out);
endmodule
