// Logisim project NguyenThiHuyenTran_6651071080_3c.circ as structural Verilog: 2 circuits, main circuit main
module main (
  input  [3:0] in_1,
  output [3:0] out_2
);

  wire CLK_out;

  Clock CLK (.out(CLK_out));
  Register #(.width(4)) register_1 (.D(in_1), .en(1'b1), .Q(out_2), .clk(CLK_out), .clr(1'b0));
endmodule

module bct_3a (
  input  E,
  input  D,
  output Q
);

  wire and_1_out, and_2_out, not_1_out, not_2_out;

  not not_1 (not_1_out, E);
  not not_2 (not_2_out, D);
  and and_1 (and_1_out, not_1_out, not_2_out);
  and and_2 (and_2_out, E, D);
  or or_1 (Q, and_1_out, and_2_out);
endmodule
