// Logisim project NguyenThiHuyenTran_6651071080_bai2.circ as structural Verilog: 2 circuits, main circuit main
module main (
  input  in_1,
  input  in_2,
  output out_3,
  output out_4,
  output out_5,
  output out_6,
  output out_7,
  output out_8,
  output out_9
);

  and and_1 (out_3, in_1, in_2);
  or or_1 (out_4, in_1, in_2);
  not not_1 (out_5, in_1);
  xor xor_1 (out_6, in_1, in_2);
  nand nand_1 (out_8, in_1, in_2);
  nor nor_1 (out_9, in_1, in_2);
  xnor xnor_1 (out_7, in_1, in_2);
endmodule

module Bang_chan_tri (
  input  A,
  input  B,
  output AB,
  output A_OR_B,
  output NOT_A,
  output A_XOR_B,
  output A_XNOR_B,
  output A_NAND_B,
  output A_NOR_B
);

  wire and_2_out, and_3_out, and_4_out, and_5_out, not_2_out, not_3_out, not_4_out, not_5_out, not_6_out,
       not_7_out, not_8_out, not_9_out;

  and and_1 (AB, A, B);
  or or_1 (A_OR_B, B, A);
  not not_1 (NOT_A, A);
  not not_2 (not_2_out, A);
  not not_3 (not_3_out, B);
  not not_4 (not_4_out, A);
  not not_5 (not_5_out, B);
  not not_6 (not_6_out, A);
  not not_7 (not_7_out, B);
  not not_8 (not_8_out, A);
  not not_9 (not_9_out, B);
  and and_2 (and_2_out, not_2_out, B);
  and and_3 (and_3_out, A, not_3_out);
  and and_4 (and_4_out, not_4_out, not_5_out);
  and and_5 (and_5_out, A, B);
  or or_2 (A_NAND_B, not_6_out, not_7_out);
  and and_6 (A_NOR_B, not_8_out, not_9_out);
  or or_3 (A_XOR_B, and_2_out, and_3_out);
  or or_4 (A_XNOR_B, and_4_out, and_5_out);
endmodule
