// Logisim project NguyenThiHuyenTran_6651071080_bai4.circ as structural Verilog: 2 circuits, main circuit main
module main (
  input  A,
  input  B,
  input  C,
  output F
);

  wire and_1_out;

  and and_1 (and_1_out, A, B);
  or or_1 (F, and_1_out, C);
endmodule

module bct_3a (
  input  E,
  input  D,
  output Q
);

  wire and_1_out, and_2_out, not_1_out, not_2_out;

  not not_1 (not_1_out, E);
  not not_2 (not_2_out, D);
  and and_1 (and_1_out, not_1_out, not_2_out);
  and and_2 (and_2_out, E, D);
  or or_1 (Q, and_1_out, and_2_out);
endmodule
