// Logisim project NguyenThiHuyenTran_6651071080_bai5.circ as structural Verilog: 3 circuits, main circuit main
module main (
  input  A,
  input  B,
  input  C,
  output F
);

  wire and_1_out;

  and and_1 (and_1_out, A, B);
  or or_1 (F, and_1_out, C);
endmodule

module bct_3a (
  input  E,
  input  D,
  output Q
);

  wire and_1_out, and_2_out, not_1_out, not_2_out;

  not not_1 (not_1_out, E);
  not not_2 (not_2_out, D);
  and and_1 (and_1_out, not_1_out, not_2_out);
  and and_2 (and_2_out, E, D);
  or or_1 (Q, and_1_out, and_2_out);
endmodule

module BAI1 (
  input  D3,
  input  D2,
  input  D1,
  input  D0,
  output Q3,
  output Q2,
  output Q1,
  output Q0
);

  wire clock_1_out;
  wire [3:0] register_1_q;

  Clock clock_1 (.out(clock_1_out));
  Register #(.width(4)) register_1 (.D({D3, D2, D1, D0}), .en(1'b1), .Q(register_1_q), .clk(clock_1_out), .clr(1'b0));
  Adder #(.width(4)) adder_1 (.a(4'b0010), .b(register_1_q), .out({Q3, Q2, Q1, Q0}));  // open: cin, cout
endmodule
